// Logisim project tf_arqui.circ as structural Verilog: 4 circuits, main circuit CPU
module CPU (
);

  wire clock_1_out, reset;
  wire [7:0] adder_1_out, PC_q, rom_1_data;

  Clock clock_1 (.out(clock_1_out));
  Register PC (.D(adder_1_out), .en(1'b1), .clk(clock_1_out), .Q(PC_q), .clr(reset));
  Adder adder_1 (.a(8'h1), .b(PC_q), .out(adder_1_out));  // open: cin, cout
  ROM rom_1 (.addr(PC_q), .data(rom_1_data));
  bancoRegistrador bancoregistrador_1 ();  // open: RegValue, RegA, RegB, Reset, RegWrite, SaidaA, SaidaB
  controle controle_1 ();  // open: in_1, UlaControl, BranchType, r0, MemRead, MemWrite, MuxWrite, MuxUla, RegWrite
endmodule

module bancoRegistrador (
  input  [7:0] RegValue,
  input  [1:0] RegA,
  input  [1:0] RegB,
  input  Reset,
  output [7:0] SaidaA,
  output [7:0] SaidaB,
  output RegWrite
);

  wire clock_1_out, demultiplexer_1_out0, demultiplexer_1_out1, demultiplexer_1_out2, demultiplexer_1_out3;
  wire [7:0] r0_q, r1_q, r2_q, r3_q;

  Demultiplexer #(.select(2)) demultiplexer_1 (
    .out0(demultiplexer_1_out0), .out1(demultiplexer_1_out1), .out2(demultiplexer_1_out2),
    .out3(demultiplexer_1_out3), .in(RegWrite), .sel(RegA));
  Register r0 (.D(RegValue), .en(demultiplexer_1_out0), .clk(clock_1_out), .Q(r0_q), .clr(Reset));
  Register r1 (.D(RegValue), .en(demultiplexer_1_out1), .clk(clock_1_out), .Q(r1_q), .clr(Reset));
  Clock clock_1 (.out(clock_1_out));
  Register r2 (.D(RegValue), .en(demultiplexer_1_out2), .clk(clock_1_out), .Q(r2_q), .clr(Reset));
  Register r3 (.D(RegValue), .en(demultiplexer_1_out3), .clk(clock_1_out), .Q(r3_q), .clr(Reset));
  Multiplexer #(.select(2), .width(8)) multiplexer_1 (
    .in0(r0_q), .in1(r1_q), .in2(r2_q), .in3(r3_q), .out(SaidaA), .sel(RegA));
  Multiplexer #(.select(2), .width(8)) multiplexer_2 (
    .in0(r0_q), .in1(r1_q), .in2(r2_q), .in3(r3_q), .out(SaidaB), .sel(RegB));
endmodule

module Ula (
  input  [7:0] A,
  input  [7:0] B,
  input  [2:0] OpULA,
  output zero,
  output [7:0] saida
);

  wire [2:0] bit_extender_1_out;
  wire [7:0] adder_1_out, and_1_out, not_1_out, or_1_out, shifter_1_out, shifter_2_out, subtractor_1_out;

  assign not_1_out = ~B;  // NOT_Gate not_1, 8 bits wide
  Bit_Extender #(.out_width(3)) bit_extender_1 (.in(B), .out(bit_extender_1_out));
  Adder adder_1 (.a(A), .b(B), .out(adder_1_out));  // open: cin, cout
  Subtractor subtractor_1 (.a(A), .b(B), .out(subtractor_1_out));  // open: bin, bout
  assign and_1_out = A & B;  // AND_Gate and_1, 8 bits wide
  assign or_1_out = A | B;  // OR_Gate or_1, 8 bits wide
  Shifter shifter_1 (.in(A), .\dist (bit_extender_1_out), .out(shifter_1_out));
  Shifter shifter_2 (.in(A), .\dist (bit_extender_1_out), .out(shifter_2_out));
  Multiplexer #(.select(3), .width(8)) multiplexer_1 (
    .in0(adder_1_out), .in1(subtractor_1_out), .in2(and_1_out), .in3(or_1_out), .in4(not_1_out),
    .in5(shifter_1_out), .in6(shifter_2_out), .out(saida), .sel(OpULA));  // open: in7
  Comparator comparator_1 (.a({8{1'b0}}), .b(saida), .eq(zero));  // open: gt, lt
endmodule

module controle (
  input  [3:0] in_1,
  output [2:0] UlaControl,
  output [1:0] BranchType,
  output r0,
  output MemRead,
  output MemWrite,
  output [1:0] MuxWrite,
  output [1:0] MuxUla,
  output RegWrite
);

  wire clock_1_out;
  wire [15:13] rom_1_data;

  Register #(.width(4)) ProvaIn (.D(in_1), .en(1'b1), .clk(clock_1_out));  // open: Q, clr
  Clock clock_1 (.out(clock_1_out));
  ROM #(.addrWidth(4), .dataWidth(16)) rom_1 (
    .addr(in_1),
    .data({rom_1_data, RegWrite, MuxUla, MuxWrite, MemWrite, MemRead, r0, BranchType, UlaControl}));
  Register #(.width(16)) ProvaOut (
    .D({rom_1_data, RegWrite, MuxUla, MuxWrite, MemWrite, MemRead, r0, BranchType, UlaControl}), .en(1'b1),
    .clk(clock_1_out));  // open: Q, clr
endmodule
